// Digital circuit alu.dig as structural Verilog
module alu (
  input  [7:0] B,
  input  [3:0] flags,
  input  [2:0] op,
  input  [7:0] A,
  output [3:0] fl,
  output [7:0] out
);

  wire [7:0] ADD, AND, not_1_out, OR, SHR, SUB;

  assign not_1_out = ~B;  // Not not_1, 8 bits wide
  BarrelShifter #(.Bits(8), .direction("right")) barrelshifter_1 (.in(B), .shift(4'b0001), .out(SHR));
  Add #(.Bits(8)) add_1 (.a(A), .b(B), .c_i(1'b0), .s(ADD));  // open: c_o
  Add #(.Bits(8)) add_2 (.a(A), .b(not_1_out), .c_i(1'b1), .s(SUB));  // open: c_o
  assign AND = B & A;  // And and_1, 8 bits wide
  assign OR = B | A;  // Or or_1, 8 bits wide
  nor nor_1 (fl[2], out[0], out[1], out[2], out[3], out[4], out[5], out[6], out[7]);
  Multiplexer #(.Selector_Bits(3), .Bits(8)) multiplexer_1 (
    .sel(op), .in_0(A), .in_1(B), .in_2(ADD), .in_3(SUB), .in_4(AND), .in_5(OR), .in_6(SHR),
    .in_7({8{1'b1}}), .out(out));

  // Other names for the same wires on the sheet: C = flags[0]; N = flags[1]; V = flags[3]; Z = fl[2]
endmodule
