// Digital circuit computer.dig as structural Verilog
module computer (
  input  clk
);

  wire demultiplexer_3_out_2, demultiplexer_3_out_3, demultiplexer_4_out_2, demultiplexer_4_out_3, IO_OE,
       IO_WE, KEYBOARD_OE, MEM_OE, MEM_WE, RAM_OE, RAM_WE, ROM_OE, ROM_WE, TERMINAL_WE;
  wire [1:0] MEM_SEL;
  wire [7:0] DBUS_I, DBUS_O;
  wire [13:0] MEM_ADDR;
  wire [15:8] keyboard_1_d;

  Demultiplexer #(.Selector_Bits(4)) demultiplexer_1 (
    .sel(MEM_ADDR[3:0]), .in(IO_WE), .out_0(TERMINAL_WE));  // open: out_1, out_2, out_3, out_4, out_5, out_6, out_7, out_8, out_9, out_10, out_11, out_12, out_13, out_14, out_15
  Demultiplexer #(.Selector_Bits(4)) demultiplexer_2 (
    .sel(MEM_ADDR[3:0]), .in(IO_OE), .out_0(KEYBOARD_OE));  // open: out_1, out_2, out_3, out_4, out_5, out_6, out_7, out_8, out_9, out_10, out_11, out_12, out_13, out_14, out_15
  main main_1 (.C(clk), .DBUS(DBUS_I), .ABUS({MEM_SEL, MEM_ADDR}), .DBUS_O(DBUS_O), .MEM_OE(MEM_OE), .MEM_WE(MEM_WE));
  Keyboard keyboard_1 (.C(clk), .en(KEYBOARD_OE), .D({keyboard_1_d, DBUS_I}));  // open: av
  ROM #(.AddrBits(14), .Bits(8)) rom_1 (.A(MEM_ADDR), .sel(ROM_OE), .D(DBUS_I));
  RAMDualPort #(.AddrBits(14), .Bits(8)) ramdualport_1 (
    .A(MEM_ADDR), .Din(DBUS_O), .str(RAM_WE), .C(clk), .ld(RAM_OE), .D(DBUS_I));
  Terminal terminal_1 (.D(DBUS_O), .C(clk), .en(TERMINAL_WE));
  or or_1 (RAM_WE, demultiplexer_3_out_2, demultiplexer_3_out_3);
  or or_2 (RAM_OE, demultiplexer_4_out_2, demultiplexer_4_out_3);
  Demultiplexer #(.Selector_Bits(2)) demultiplexer_3 (
    .sel(MEM_SEL), .in(MEM_WE), .out_0(ROM_WE), .out_1(IO_WE), .out_2(demultiplexer_3_out_2),
    .out_3(demultiplexer_3_out_3));
  Demultiplexer #(.Selector_Bits(2)) demultiplexer_4 (
    .sel(MEM_SEL), .in(MEM_OE), .out_0(ROM_OE), .out_1(IO_OE), .out_2(demultiplexer_4_out_2),
    .out_3(demultiplexer_4_out_3));

  // Notes on the sheet:
  //   clk: Hz: 2147483647
  //   contents of rom_1 (hex, n*v repeats v):
  //   48,24,1,48,0,2,6e,0,73,28,48,0,4,1c,b,68,11,8b,40,0,9,50,1,1,6c
  //   ,2,6e,4,a,50,1,2,6e,e6,6e,fe,70,72,69,6e,74,66,20,72,75,6c,65
  //   ,73,21
endmodule
